# Fritzing sketch rampart (saved by Fritzing 0.9.3b)
circuit board: 6.1cm x 5.2cm
breadboards: 1

parts:
  Nano = Arduino Nano (Rev3.0)
  10k = Rotary Potentiometer (Small) [maximum_resistance=100kΩ package=THT]
  J1 = Piezo Speaker
  10K = Rotary Potentiometer (Small) [maximum_resistance=100kΩ package=THT]
  10k_2 = Rotary Potentiometer (Small) [maximum_resistance=100kΩ package=THT]
  J2 = female pin header, 4 pins [form="♀ (female)"]
  10k_3 = Rotary Potentiometer (Small) [maximum_resistance=100kΩ package=THT]
  5K = Resistor [tolerance=±1% resistance=4.7k package=THT]
  5K_2 = Resistor [tolerance=±5% resistance=4.7k package=THT]
  S2 = Pushbutton [package="[THT]"]
  S3 = Pushbutton [package="[THT]"]
  J3 = female pin header, 4 pins [form="♀ (female)"]
  J4 = female pin header, 4 pins [form="♀ (female)"]
  5K_3 = Resistor [tolerance=±5% resistance=4.7k package=THT]
  5K_4 = Resistor [tolerance=±5% resistance=4.7k package=THT]
  5k = Resistor [tolerance=±5% resistance=4.7k package=THT]
  5k_2 = Resistor [tolerance=±5% resistance=4.7k package=THT]
  J5 = female pin header, 4 pins [form="♀ (female)"]
  10K1 = Rotary Potentiometer (Small) [maximum_resistance=100kΩ package=THT]
  J7 = female pin header, 2 pins [form="♀ (female)"]
  J8 = female pin header, 2 pins [form="♀ (female)"]
  J6 = female pin header, 2 pins [form="♀ (female)"]
  J10 = female pin header, 2 pins [form="♀ (female)"]
  J11 = female pin header, 2 pins [form="♀ (female)"]
  100n = Ceramic Capacitor [capacitance="100 nF" package="100 mil [THT, multilayer]"]
  1uf = Electrolytic Capacitor [capacitance=1μF package="100 mil [THT, electrolytic]"]

nets:
  N1: Nano.D1/TX, J7.pin2
  N2: Nano.D0/RX, J7.pin1
  N3: Nano.GND, 10k.leg1, J1.pin1, 10K.leg1, 10k_2.leg1, 10k_3.leg1, 5K.Pin_0, 5K_2.Pin_0, 5K_3.Pin_1, 5K_4.Pin_1, 5k.Pin_1, 5k_2.Pin_1, J6.pin1, J10.pin1, J10.pin2, 100n.0, 1uf.-
  N4: Nano.D2, 5K.Pin_1, S3.Pin_3, S3.Pin_4
  N5: Nano.D3, 5K_2.Pin_1, S2.Pin_3, S2.Pin_4
  N6: Nano.D4, J8.pin2
  N7: Nano.D5, J8.pin1
  N8: Nano.D9, 10K1.wiper
  N9: Nano.VIN, J11.pin1, J11.pin2
  N10: Nano.5V, 10k.leg2, 10K.leg2, 10k_2.leg2, 10k_3.leg2, S2.Pin_1, S2.Pin_2, S3.Pin_1, S3.Pin_2, J4.pin1, J4.pin2, J4.pin3, J4.pin4
  N11: Nano.A7, J2.pin4, J5.pin4
  N12: Nano.A6, J2.pin3, J5.pin3
  N13: Nano.A5, J2.pin2, J5.pin2
  N14: Nano.A4, J2.pin1, J5.pin1
  N15: Nano.A3, 10K.wiper
  N16: Nano.A2, 10k_3.wiper
  N17: Nano.A1, 10k_2.wiper
  N18: Nano.A0, 10k.wiper
  N19: J1.pin2, 10K1.leg1, J6.pin2, 100n.1
  N20: J3.pin1, 5K_3.Pin_0
  N21: J3.pin2, 5K_4.Pin_0
  N22: J3.pin3, 5k.Pin_0
  N23: J3.pin4, 5k_2.Pin_0
  N24: 10K1.leg2, 1uf.+

notes:
  rampart v1
