# Fritzing sketch rampart2 (saved by Fritzing 0.9.3b)
circuit board: 6.1cm x 5.2cm
breadboards: 1

parts:
  10k = Rotary Potentiometer (Small) [maximum_resistance=100kΩ package=THT]
  J1 = Piezo Speaker
  10K = Rotary Potentiometer (Small) [maximum_resistance=100kΩ package=THT]
  10k_2 = Rotary Potentiometer (Small) [maximum_resistance=100kΩ package=THT]
  J2 = female pin header, 4 pins [form="♀ (female)"]
  10k_3 = Rotary Potentiometer (Small) [maximum_resistance=100kΩ package=THT]
  5K = Resistor [tolerance=±1% resistance=4.7k package=THT]
  5K_2 = Resistor [tolerance=±5% resistance=4.7k package=THT]
  S2 = Pushbutton [package="[THT]"]
  S3 = Pushbutton [package="[THT]"]
  J3 = female pin header, 4 pins [form="♀ (female)"]
  J4 = female pin header, 4 pins [form="♀ (female)"]
  5K_3 = Resistor [tolerance=±5% resistance=4.7k package=THT]
  5K_4 = Resistor [tolerance=±5% resistance=4.7k package=THT]
  5k = Resistor [tolerance=±5% resistance=4.7k package=THT]
  5k_2 = Resistor [tolerance=±5% resistance=4.7k package=THT]
  J5 = female pin header, 4 pins [form="♀ (female)"]
  10K1 = Rotary Potentiometer (Small) [maximum_resistance=100kΩ package=THT]
  J8 = female pin header, 2 pins [form="♀ (female)"]
  J6 = female pin header, 2 pins [form="♀ (female)"]
  100n = Ceramic Capacitor [capacitance="100 nF" package="100 mil [THT, multilayer]"]
  1uf = Electrolytic Capacitor [capacitance=1μF package="100 mil [THT, electrolytic]"]
  J10 = female pin header, 2 pins [form="♀ (female)"]
  5K_5 = Resistor [tolerance=±5% resistance=4.7k package=THT]
  S4 = Pushbutton [package="[THT]"]
  LED1 = LED - 3mm [color="Red (633nm)" package="3 mm [THT]"]
  5K2 = Resistor [tolerance=±5% resistance=4.7k package=THT]
  J11 = female pin header, 2 pins [form="♀ (female)"]
  J12 = female pin header, 1 pin [form="♀ (female)"]
  Nano = Arduino Nano (Rev3.0)
  J13 = female pin header, 2 pins [form="♀ (female)"]
  J14 = female pin header, 2 pins [form="♀ (female)"]

nets:
  N1: 10k.leg1, J1.pin1, 10K.leg1, 10k_2.leg1, 10k_3.leg1, 5K.Pin_0, 5K_2.Pin_0, 5K_3.Pin_1, 5K_4.Pin_1, 5k.Pin_1, 5k_2.Pin_1, J6.pin1, 100n.0, 1uf.-, J10.pin1, 5K_5.Pin_0, 5K2.Pin_1, Nano.GND, J13.pin1
  N2: 10k.wiper, Nano.A0
  N3: 10k.leg2, 10K.leg2, 10k_2.leg2, 10k_3.leg2, S2.Pin_1, S2.Pin_2, S3.Pin_1, S3.Pin_2, J4.pin1, J4.pin2, J4.pin3, J4.pin4, S4.Pin_1, S4.Pin_2, J12.pin1, Nano.5V
  N4: J1.pin2, 10K1.leg1, J6.pin2, 100n.1
  N5: 10K.wiper, Nano.A3
  N6: 10k_2.wiper, Nano.A1
  N7: J2.pin1, J5.pin1, Nano.A4
  N8: J2.pin2, J5.pin2, Nano.A5
  N9: J2.pin3, J5.pin3, Nano.A6
  N10: J2.pin4, J5.pin4, Nano.A7
  N11: 10k_3.wiper, Nano.A2
  N12: 5K.Pin_1, S3.Pin_3, S3.Pin_4, Nano.D1/TX
  N13: 5K_2.Pin_1, S2.Pin_3, S2.Pin_4, Nano.D0/RX
  N14: J3.pin1, 5K_3.Pin_0
  N15: J3.pin2, 5K_4.Pin_0
  N16: J3.pin3, 5k.Pin_0
  N17: J3.pin4, 5k_2.Pin_0
  N18: 10K1.wiper, Nano.D9
  N19: 10K1.leg2, 1uf.+
  N20: J8.pin1, J8.pin2, Nano.D5
  N21: J10.pin2, Nano.VIN, J13.pin2
  N22: 5K_5.Pin_1, S4.Pin_3, S4.Pin_4, Nano.D4
  N23: LED1.cathode, 5K2.Pin_0
  N24: LED1.anode, Nano.D13/SCK
  N25: J11.pin1, J11.pin2, Nano.D6
  N26: Nano.D2, J14.pin2
  N27: Nano.D3, J14.pin1

notes:
  rampart v1
