# Fritzing sketch rampart3 (saved by Fritzing 1.0.2b)
circuit board: 8.79cm x 6.5cm
breadboards: 2

parts:
  10k = Rotary Potentiometer (Small) [maximum_resistance=100kΩ knob_status=50% power=0.5W package=THT]
  10k_2 = Rotary Potentiometer (Small) [maximum_resistance=100kΩ knob_status=50% power=0.5W package=THT]
  10k_3 = Rotary Potentiometer (Small) [maximum_resistance=100kΩ knob_status=50% power=0.5W package=THT]
  S3 = Pushbutton [package="[THT]"]
  S2 = Pushbutton [package="[THT]"]
  J3 = female pin header, 4 pins [form="♀ (female)"]
  J4 = female pin header, 4 pins [form="♀ (female)"]
  1K = Resistor [tolerance=±5% resistance=4.7k power=0.25W package=THT]
  1K_2 = Resistor [tolerance=±5% resistance=1k power=0.25W package=THT]
  1k = Resistor [tolerance=±5% resistance=1k power=0.25W package=THT]
  1k_2 = Resistor [tolerance=±5% resistance=1k power=0.25W package=THT]
  J10 = female pin header, 2 pins [form="♀ (female)"]
  J6 = female pin header, 2 pins [form="♀ (female)"]
  LED1 = LED - 3mm [color="Red (633nm)" current=0.030A package="3 mm [THT]"]
  4_7k = Resistor [tolerance=±5% resistance=4.7k power=0.25W package=THT]
  J11 = female pin header, 2 pins [form="♀ (female)"]
  Nano = Arduino Nano (Rev3.0)
  Power_plug2 = Power plug
  104 = Capacitor [package=cap-pth-5mm]
  105 = Capacitor [package=cap-pth-5mm]
  10K2 = Rotary Potentiometer (Small) [maximum_resistance=10kΩ knob_status=50% power=0.5W package=THT]
  100Ω1 = Resistor [tolerance=±5% power=0.25 resistance=100 package=THT]
  10K3 = Resistor [tolerance=±5% power=0.25 resistance=10k package=THT]
  100Ω2 = Resistor [tolerance=±5% power=0.25 resistance=100 package=THT]
  Audio_OUt1 = Audio Jack (TRS) 3.5mm [package="PG203J [THT]"]
  clckaudio1 = Audio Jack (TRS) 3.5mm [package="PG203J [THT]"]
  1KΩ1 = Resistor [tolerance=±5% resistance=1k power=0.25W package=THT]
  SSD1307 = OLED Mono 0.56 inch blue or white
  J2 = female pin header, 3 pins [form="♀ (female)"]
  J5 = female pin header, 3 pins [form="♀ (female)"]
  J12 = female pin header, 2 pins [form="♀ (female)"]
  RE1 = Rotary Encoder [package=THT]
  VCC1 = 4 x AAA Battery Mount
  J9 = female pin header, 2 pins [form="♀ (female)"]
  S5 = SPST Switch [package=switch-spdt_kit]

nets:
  GND: 10k.leg1, 10k_2.leg1, 10k_3.leg1, S3.Pin_1, S3.Pin_2, S2.Pin_1, S2.Pin_2, 1K.Pin_1, 1K_2.Pin_1, 1k.Pin_1, 1k_2.Pin_1, J6.pin1, 4_7k.Pin_1, Nano.GND, Power_plug2.GND, 104.1, 10K3.Pin_1, Audio_OUt1.Sleeve, clckaudio1.Sleeve, SSD1307.GND, RE1.GND, RE1.SW-2, VCC1.-
  N1: 10k.wiper, Nano.A0
  V++: 10k.leg2, 10k_2.leg2, 10k_3.leg2, J4.pin1, J4.pin2, J4.pin3, J4.pin4, Nano.5V, SSD1307.VCC
  N2: 10k_2.wiper, Nano.A1
  N3: 10k_3.wiper, Nano.A2
  N4: S3.Pin_3, S3.Pin_4, Nano.D3
  N5: S2.Pin_3, S2.Pin_4, Nano.D2
  N6: J3.pin1, 1K.Pin_0
  N7: J3.pin2, 1K_2.Pin_0
  N8: J3.pin3, 1k.Pin_0
  N9: J3.pin4, 1k_2.Pin_0
  N10: J10.pin1, J10.pin2, Nano.D10
  N11: J6.pin2, 10K2.leg1
  N12: LED1.cathode, 4_7k.Pin_0
  N13: LED1.anode, Nano.D13/SCK
  N14: J11.pin1, J11.pin2, Nano.D11/MOSI
  N15: Nano.D1/TX, 1KΩ1.Pin_0
  N16: Nano.D4, RE1.SW-1
  N17: Nano.D5, RE1.Pin-B
  N18: Nano.D6, RE1.Pin-A
  N19: Nano.D9, 105.1, J9.pin1, J9.pin2
  N20: Nano.D12/MISO, J12.pin1, J12.pin2
  N21: Nano.VIN, S5.O
  N22: Nano.A7, J2.pin3, J5.pin3
  N23: Nano.A6, J2.pin2, J5.pin2
  N24: Nano.A5, SSD1307.SCL
  N25: Nano.A4, SSD1307.SDA
  N26: Nano.A3, J2.pin1, J5.pin1
  N27: Power_plug2.VCC, VCC1.+, S5.P
  N28: 104.2, 10K2.leg2, 100Ω1.Pin_1
  N29: 105.2, 10K3.Pin_0, 100Ω2.Pin_1
  N30: 10K2.wiper, 100Ω2.Pin_0
  N31: 100Ω1.Pin_0, Audio_OUt1.Ring, Audio_OUt1.Tip, clckaudio1.Ring
  N32: clckaudio1.Tip, 1KΩ1.Pin_1

notes:
  rampart v3
  blueprint@poetaster.de 2024

custom parts:
  OLED Mono 0.56 inch blue or white: OLED, I2C 3.3V - 5V Blue and White text versions
  Rotary Encoder: Rotary Encoder with push button
