# Fritzing sketch rampart_pico (saved by Fritzing 1.0.6)
circuit board: 8.80001cm x 6.50001cm
breadboards: 2

parts:
  10k = Rotary Potentiometer (Small) [maximum_resistance=100kΩ knob_status=50% power=0.5W package=THT]
  10k_2 = Rotary Potentiometer (Small) [maximum_resistance=100kΩ knob_status=50% power=0.5W package=THT]
  10k_3 = Rotary Potentiometer (Small) [maximum_resistance=100kΩ knob_status=50% power=0.5W package=THT]
  -/+ = female pin header, 2 pins [form="♀ (female)"]
  104 = Capacitor [package=cap-pth-5mm]
  105 = Capacitor [package=cap-pth-5mm]
  10K2 = Rotary Potentiometer (Small) [maximum_resistance=10kΩ knob_status=50% power=0.5W package=THT]
  100Ω = Resistor [tolerance=±5% power=0.25 resistance=100 package=THT]
  10K = Resistor [tolerance=±5% power=0.25 resistance=10k package=THT]
  100Ω_2 = Resistor [tolerance=±5% power=0.25 resistance=100 package=THT]
  audio> = Audio Jack (TRS) 3.5mm [package="PG203J [THT]"]
  SSD1307 = OLED Mono 0.56 inch blue or white
  J2 = female pin header, 3 pins [form="♀ (female)"]
  J5 = female pin header, 3 pins [form="♀ (female)"]
  RE1 = Rotary Encoder [package=THT]
  TXRX = female pin header, 2 pins [form="♀ (female)"]
  1uF = Electrolytic Capacitor [capacitance=1µF voltage=35V package="100 mil [THT, electrolytic]"]
  pico2zero = Waveshare rp2040-zero tht [package=THT]
  J14 = 3.5mm Audio Jack-wq-pj320b.fzpz [package=audio-jack-3.5mm-smd]  # not connected
  J15 = 3.5mm Audio Jack-wq-pj320b.fzpz [package=audio-jack-3.5mm-smd]
  ADS1115 = female pin header, 10 pins [form="♀ (female)"]
  v+ = female pin header, 3 pins [form="♀ (female)"]
  v- = female pin header, 3 pins [form="♀ (female)"]
  10K_2 = Resistor [tolerance=±5% resistance=10k power=0.25W package=THT]
  10k1 = Resistor [tolerance=±5% resistance=10k power=0.25W package=THT]
  2N3904 = NPN-Transistor [package="TO92 [THT]"]
  J8/9 = female pin header, 2 pins [form="♀ (female)"]
  J13 = female pin header, 7 pins [form="♀ (female)"]

nets:
  GND: 10k.leg1, 10k_2.leg1, 10k_3.leg1, -/+.pin1, 104.1, 10K.Pin_1, audio>.Sleeve, SSD1307.GND, RE1.GND, RE1.SW-2, 1uF.-, pico2zero.Pin_2, J15.pin_4, ADS1115.pin2, v-.pin1, v-.pin2, v-.pin3, 10k1.Pin_1, 2N3904.E, J13.pin2
  N1: 10k.wiper, pico2zero.Pin_4
  N2: 10k.leg2, 10k_2.leg2, 10k_3.leg2, SSD1307.VCC, pico2zero.Pin_3, ADS1115.pin1, v+.pin1, v+.pin2, v+.pin3, J8/9.pin2, J13.pin1
  N3: 10k_2.wiper, pico2zero.Pin_5
  N4: 10k_3.wiper, pico2zero.Pin_6
  N5: -/+.pin2, 10K2.leg1, 1uF.+
  N6: 104.2, 10K2.leg2, 100Ω.Pin_1
  N7: 105.1, pico2zero.Pin_12
  N8: 105.2, 10K.Pin_0, 100Ω_2.Pin_1, J15.Pin_3
  N9: 10K2.wiper, 100Ω_2.Pin_0
  N10: 100Ω.Pin_0, audio>.Ring, audio>.Tip
  N11: SSD1307.SDA, pico2zero.Pin_20
  N12: SSD1307.SCL, pico2zero.Pin_19
  N13: J2.pin1, J5.pin1, ADS1115.pin7
  N14: J2.pin2, J5.pin2, ADS1115.pin8
  N15: J2.pin3, J5.pin3, ADS1115.pin9
  N16: RE1.Pin-A, pico2zero.Pin_11
  N17: RE1.Pin-B, pico2zero.Pin_10
  N18: RE1.SW-1, pico2zero.Pin_16
  N19: TXRX.pin1, pico2zero.Pin_23
  N20: TXRX.pin2, pico2zero.Pin_22, 10k1.Pin_0, 2N3904.C
  N21: pico2zero.Pin_7, J8/9.pin1
  N22: pico2zero.Pin_8, ADS1115.pin3
  N23: pico2zero.Pin_9, ADS1115.pin4
  N24: pico2zero.Pin_13, J13.pin3
  N25: pico2zero.Pin_14, J13.pin4
  N26: pico2zero.Pin_15, J13.pin5
  N27: pico2zero.Pin_17, J13.pin6
  N28: pico2zero.Pin_18, J13.pin7
  N29: J15.pin_2, 10K_2.Pin_0
  N30: 10K_2.Pin_1, 2N3904.B

notes:
  rampart pico
  blueprint@poetaster.de 2026

custom parts:
  OLED Mono 0.56 inch blue or white: OLED, I2C 3.3V - 5V Blue and White text versions
  Rotary Encoder: Rotary Encoder with push button
  Waveshare rp2040-zero tht: .RP2040-Zero, A Low-Cost, High-Performance Pico-Like MCU Board Based On Raspberry Pi Microcontroller RP2040. This varant is THT without the extra connections.
  3.5mm Audio Jack-wq-pj320b.fzpz: 3.5mm Audio Jack WQP-PJ320B is a SMD jack, dia 1/8 inch, female, right angle and through hole.
